// Digital circuit CPU.dig as structural Verilog
module CPU (
  input  Clk,
  input  Rst,
  input  [7:0] Data_Bus,
  output [7:0] A,
  output [7:0] B,
  output [7:0] CH,
  output [7:0] CL,
  output [7:0] MH,
  output [7:0] ML,
  output [7:0] IR,
  output [3:0] Step,
  output [15:0] Address_Bus,
  output Ro,
  output Ri,
  output Boot,
  output [7:0] Bank,
  output CF
);

  wire alu_1_f, Boot_t, CE, ci, done, EI, inv, MA, ME, nAi, nand_1_out, nand_2_out, nAo, nBi, nBo, nCHi,
       nCHo, nCLi, nCLo, nIi, nMHi, nMLi, \nor , not_1_out, nPo, nRi, nSo, OS0, OS1, OS2, Rst_t;
  wire [3:0] count_4_1_q;
  wire [6:0] IR_q;
  wire [7:0] A_q, alu_1_q, B_q, MAR_qh, MAR_ql;
  wire [15:0] PC_ql;

  nand nand_1 (nand_1_out, done, done);
  RS_FF_AS rs_ff_as_1 (.S(~nand_1_out), .R(~Rst), .Q(Boot), .nQ(Boot_t));
  bus_control bus_control_1 (.inv(inv), .OS0(OS0), .OS1(OS1), .OS2(OS2), .boot(Boot_t), .Q(Data_Bus));
  \reg  u_A (.D(Data_Bus), .Clk(Clk), .En(nAi), .V(A), .Q(A_q));
  nand nand_2 (nand_2_out, Boot_t, done);
  driver driver_1 (.En(nAo), .D(A_q), .Q(Data_Bus));
  count_16 PC (
    .D(Data_Bus), .JL(nCLi), .JH(nCHi), .En(CE), .Clk(Clk), .Rst(Rst_t), .QL(PC_ql[7:0]), .VL(CL),
    .QH(PC_ql[15:8]), .VH(CH), .Co(done));
  \reg  u_B (.D(Data_Bus), .Clk(Clk), .En(nBi), .V(B), .Q(B_q));
  driver driver_2 (.En(nCLo), .D(PC_ql[7:0]), .Q(Data_Bus));
  and and_1 (Rst_t, nand_2_out, Rst);
  driver driver_3 (.En(nBo), .D(B_q), .Q(Data_Bus));
  driver driver_4 (.En(nCHo), .D(PC_ql[15:8]), .Q(Data_Bus));
  PullUp pullup_1 (.out(EI));
  ALU alu_1 (.A(A_q), .B(B_q), .inv(inv), .ci(ci), .\nor (\nor ), .Zero(ME), .Q(alu_1_q), .F(alu_1_f));
  PullDown pulldown_1 (.out(OS2));
  PullDown pulldown_2 (.out(OS1));
  count_16 MAR (
    .D(Data_Bus), .JL(nMLi), .JH(nMHi), .En(ME), .Clk(Clk), .Rst(Rst_t), .QL(MAR_ql), .VL(ML), .QH(MAR_qh),
    .VH(MH));  // open: Co
  PullDown pulldown_3 (.out(OS0));
  PullDown pulldown_4 (.out(ci));
  FLAG flag_1 (.F(alu_1_f), .Clk(Clk), .En(nSo), .CF(CF));
  driver driver_5 (.En(nSo), .D(alu_1_q), .Q(Data_Bus));
  PullDown pulldown_5 (.out(inv));
  PullUp pullup_2 (.out(CE));
  Multiplexer #(.Bits(16)) multiplexer_1 (.sel(MA), .in_0(PC_ql), .in_1({MAR_qh, MAR_ql}), .out(Address_Bus));
  PullDown pulldown_6 (.out(ME));
  PullDown pulldown_7 (.out(MA));
  count_4 count_4_1 (.Clr(EI), .Clk(Clk), .V(Step), .Q(count_4_1_q));
  \reg  u_IR (.D(Data_Bus), .Clk(Clk), .En(nIi), .V(IR), .Q({\nor , IR_q}));
  PullUp pullup_3 (.out(nMHi));
  PullUp pullup_4 (.out(nMLi));
  PullUp pullup_5 (.out(nCHi));
  PullUp pullup_6 (.out(nCLi));
  EEPROMDualPort #(.AddrBits(13), .Bits(16)) eepromdualport_1 (
    .A({1'b0, CF, IR_q, count_4_1_q}), .Din({16{1'b0}}), .str(1'b0), .C(1'b0), .ld(not_1_out),
    .D({EI, OS2, OS1, OS0, ci, inv, CE, ME, MA, nMHi, nMLi, nCHi, nCLi, nRi, nBi, nAi}));
  not not_1 (not_1_out, Boot_t);
  IO io_1 (.Po(nPo), .Clk(Clk), .A(Address_Bus), .D(Data_Bus), .Q(Data_Bus), .Bank(Bank));
  PullUp pullup_7 (.out(nBi));
  PullDown pulldown_8 (.out(nRi));
  PullUp pullup_8 (.out(nAi));
  control_logic control_logic_1 (
    .OS0(OS0), .OS1(OS1), .OS2(OS2), .Step(Step), .Clk(Clk), .Ri(nRi), .Ao(nAo), .Bo(nBo), .So(nSo),
    .CLo(nCLo), .CHo(nCHo), .Ro(Ro), .Ric(Ri), .Ii(nIi), .Po(nPo));

  // Notes on the sheet:
  //   Clk: Hz: 2147483647
  //   Rst: default 1
  //   contents of eepromdualport_1 (hex, n*v repeats v):
  //   727f,807f,8*7f,0,5*7f,727f,727c,807f,13*7f,727f,47d,3c7c,807f
  //   ,12*7f,727f,47d,307c,807f,12*7f,727f,727d,307c,807f,12*7f,727f
  //   ,405f,503f,71f7,70ef,807f,10*7f,727f,27f,27f,807f,12*7f,727f,405f
  //   ,503f,71f7,70ef,807f,10*7f,727f,311f,10fb,47e,307f,70fe,405f,503f
  //   ,71f7,70ef,807f,5*7f,727f,311f,10fb,47e,307f,70fe,27f,27f,807f
  //   ,7*7f,727f,725f,723f,70fd,307c,807f,10*7f,727f,725f,723f,70fd
  //   ,307c,807f,10*7f,727f,725f,723f,70fd,3c7c,807f,10*7f,727f,725f
  //   ,723f,70fd,347c,807f,10*7f,727f,725f,723f,70fc,807f,11*7f,727f
  //   ,725f,723f,10fb,807f,11*7f,727f,3f,45f,70dd,10fb,207e,45d,30fb
  //   ,105f,70fe,807f,5*7f,727f,3f,45d,70fe,3cfe,10fb,105f,70fc,807f
  //   ,7*7f,727f,47d,387f,807f,12*7f,727f,30fd,307f,807f,12*7f,727f
  //   ,725f,60fc,807f,12*7f,727f,311f,10fb,41d,70de,40fb,305e,50fb,205f
  //   ,30fb,405f,503f,71f7,70ef,311f,70fe,727f,311f,10fb,41d,70de,3c5e
  //   ,70ef,3c5e,70f7,205f,10fb,331f,72fe,807f,7f,7f,727f,107d,307c
  //   ,807f,12*7f,727f,107d,347f,8*307c,807f,4*7f,727f,807f,14*7f,727f
  //   ,107d,307c,807f,12*7f,727f,107d,8*307c,807f,5*7f,727f,727d,725f
  //   ,723f,20fb,807f,10*7f,727f,107d,307f,405f,503f,71f7,70ef,807f
  //   ,8*7f,727f,107d,307f,27f,27f,807f,10*7f,727f,725f,723f,70fd,3c7d
  //   ,807f,10*7f,727f,727d,3c7d,807f,12*7f,727f,725f,723f,71fd,70bf
  //   ,205f,70fc,807f,8*7f,727f,725f,723f,71fd,70bf,205f,10fb,807f,8*7f
  //   ,727f,41d,70de,40fb,305e,50fb,205f,30fb,405f,503f,71f7,70ef,807f
  //   ,7f,7f,7f,727f,41d,70de,3c5e,70ef,3c5e,70f7,205f,10fb,807f,6*7f
  //   ,727f,807f,14*7f,727f,807f,14*7f,727f,107d,317e,3c7c,807f,11*7f
  //   ,727f,807f,14*7f,727f,807f,14*7f,727f,807f,14*7f,727f,807f,14*7f
  //   ,727f,725f,723f,70fd,725f,723f,20fb,807f,8*7f,727f,807f,14*7f
  //   ,727f,807f,14*7f,727f,311f,10fb,725f,723f,70fc,347d,3cfb,311f
  //   ,70fe,807f,5*7f,727f,807f,14*7f,727f,807f,14*7f,727f,807f,14*7f
  //   ,727f,807f,14*7f,727f,807f,14*7f,727f,725f,723f,70fd,10fb,207e
  //   ,47d,3c7d,70fe,20fb,807f,5*7f,727f,725f,723f,70fd,10fb,47e,307d
  //   ,70fe,20fb,807f,6*7f,727f,807f,14*7f,727f,807f,14*7f,727f,807f
  //   ,14*7f,727f,807f,14*7f,727f,807f,14*7f,727f,807f,14*7f,727f,807f
  //   ,14*7f,727f,807f,14*7f,727f,807f,14*7f,727f,807f,14*7f,727f,807f
  //   ,14*7f,727f,807f,14*7f,727f,807f,14*7f,727f,807f,14*7f,727f,807f
  //   ,14*7f,727f,807f,14*7f,727f,807f,14*7f,727f,807f,14*7f,727f,807f
  //   ,14*7f,727f,807f,14*7f,727f,807f,14*7f,727f,807f,14*7f,727f,807f
  //   ,14*7f,727f,807f,14*7f,727f,807f,14*7f,727f,807f,14*7f,727f,807f
  //   ,14*7f,727f,807f,14*7f,727f,807f,14*7f,727f,807f,14*7f,727f,807f
  //   ,14*7f,727f,807f,14*7f,727f,807f,14*7f,727f,807f,14*7f,727f,807f
  //   ,14*7f,727f,807f,14*7f,727f,807f,14*7f,727f,807f,14*7f,727f,807f
  //   ,14*7f,727f,807f,14*7f,727f,807f,14*7f,727f,807f,14*7f,727f,807f
  //   ,14*7f,727f,807f,14*7f,727f,807f,14*7f,727f,807f,14*7f,727f,807f
  //   ,14*7f,727f,807f,14*7f,727f,807f,14*7f,727f,807f,14*7f,727f,807f
  //   ,14*7f,727f,807f,14*7f,727f,807f,14*7f,727f,807f,14*7f,727f,807f
  //   ,14*7f,727f,807f,14*7f,727f,807f,14*7f,727f,807f,14*7f,727f,807f
  //   ,14*7f,727f,807f,14*7f,727f,807f,14*7f,727f,807f,14*7f,727f,807f
  //   ,14*7f,727f,807f,14*7f,727f,807f,14*7f,727f,807f,14*7f,727f,707d
  //   ,311f,34fb,107d,727e,347e,70fd,307c,307c,807f,5*7f,727f,725f,723f
  //   ,70fd,307c,307c,807f,9*7f,727f,727d,307c,307c,807f,11*7f,727f
  //   ,725f,723f,10fd,307e,70fd,347c,807f,8*7f,727f,10fd,307e,727d,347c
  //   ,807f,10*7f,727f,10fd,307e,727d,347d,807f,10*7f,727f,807f,14*7f
  //   ,727f,807f,14*7f,727f,727c,807f,13*7f,727f,47d,3c7c,807f,12*7f
  //   ,727f,47d,307c,807f,12*7f,727f,727d,307c,807f,12*7f,727f,405f
  //   ,503f,71f7,70ef,807f,10*7f,727f,405f,503f,71f7,70ef,807f,10*7f
  //   ,727f,27f,27f,807f,12*7f,727f,311f,10fb,47e,307f,70fe,27f,27f
  //   ,807f,7*7f,727f,311f,10fb,47e,307f,70fe,405f,503f,71f7,70ef,807f
  //   ,5*7f,727f,725f,723f,70fd,307c,807f,10*7f,727f,725f,723f,70fd
  //   ,387c,807f,10*7f,727f,725f,723f,70fd,3c7c,807f,10*7f,727f,725f
  //   ,723f,70fd,3c7c,807f,10*7f,727f,725f,723f,70fc,807f,11*7f,727f
  //   ,725f,723f,10fb,807f,11*7f,727f,3f,45f,70dd,10fb,207e,45d,30fb
  //   ,105f,70fe,807f,5*7f,727f,3f,45d,70fe,3cfe,10fb,105f,70fc,807f
  //   ,7*7f,727f,47d,387f,807f,12*7f,727f,30fd,307f,807f,12*7f,727f
  //   ,725f,60fc,807f,12*7f,727f,311f,10fb,41d,70de,40fb,305e,50fb,205f
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endmodule
