// Digital circuit FLAG.dig as structural Verilog
module FLAG (
  input  F,
  input  Clk,
  input  En,
  output CF
);

  wire q1;

  _74377 _74377_1 (
    .pin1(En), .pin2(CF), .pin3(F), .pin4(1'b0), .pin5(q1), .pin7(1'b0), .pin8(1'b0), .pin10(1'b0),
    .pin11(Clk), .pin13(1'b0), .pin14(1'b0), .pin17(1'b0), .pin18(1'b0), .pin20(1'b1));  // open: pin6, pin9, pin12, pin15, pin16, pin19

  // Other names for the same wires on the sheet: q0 = CF
endmodule
