// Digital circuit Keyboard.dig as structural Verilog
module Keyboard (
  input  Clk,
  input  En,
  output [7:0] D
);

  wire [15:8] keyboard_1_d;

  Keyboard keyboard_1 (.C(Clk), .en(En), .D({keyboard_1_d, D}));  // open: av
endmodule
