// Digital circuit Screen Cicuitry.dig as structural Verilog
module Screen_Cicuitry (
  input  Clk,
  input  xi,
  input  yi,
  input  si,
  input  [7:0] D
);

  wire not_1_out;
  wire [7:0] x_q, y_q;

  Register #(.Bits(8)) x (.D(D), .C(Clk), .en(~xi), .Q(x_q));
  Register #(.Bits(8)) y (.D(D), .C(Clk), .en(~yi), .Q(y_q));
  not not_1 (not_1_out, si);
  GraphicCard #(.graphicHeight(128), .graphicWidth(128)) graphiccard_1 (
    .A({1'b0, y_q[6:0], x_q[6:0]}), .str(not_1_out), .C(Clk), .ld(1'b0), .B(1'b0), .D(D[0]));

  // Other names for the same wires on the sheet: Data[7:0] = D
endmodule
