// Digital circuit control logic.dig as structural Verilog
module control_logic (
  input  OS0,
  input  OS1,
  input  OS2,
  input  [3:0] Step,
  input  Clk,
  input  Ri,
  output Ao,
  output Bo,
  output So,
  output CLo,
  output CHo,
  output Ro,
  output Ric,
  output Ii,
  output Po
);

  wire _7432_1_pin3, _7432_1_pin6;
  wire [0:0] decoder_1_q;

  decoder decoder_1 (
    .A(OS0), .B(OS1), .C(OS2), .en1(1'b0), .en2(1'b0), .en3(1'b1),
    .Q({Ro, Po, CHo, CLo, So, Bo, Ao, decoder_1_q[0]}));
  _7432 _7432_1 (
    .pin1(Step[3]), .pin2(Step[2]), .pin3(_7432_1_pin3), .pin4(Step[1]), .pin5(Step[0]), .pin6(_7432_1_pin6),
    .pin7(1'b0), .pin8(Ric), .pin9(Clk), .pin10(Ri), .pin11(Ii), .pin12(_7432_1_pin3), .pin13(_7432_1_pin6),
    .pin14(1'b1));
endmodule
