// Digital circuit count-4.dig as structural Verilog
module count_4 (
  input  Clr,
  input  Clk,
  output [3:0] V,
  output [3:0] Q
);

  wire [3:0] add_1_s, delay_1_out;

  Add #(.Bits(4)) add_1 (.a(Q), .b(4'b0000), .c_i(1'b1), .s(add_1_s));  // open: c_o
  Delay #(.Bits(4), .delayTime(5)) delay_1 (.in(add_1_s), .out(delay_1_out));
  D_FF_AS #(.Bits(4)) d_ff_as_1 (.Set(1'b0), .D(delay_1_out), .C(~Clk), .Clr(Clr), .Q(Q));  // open: nQ

  assign V = Q;

  // Notes on the sheet:
  //   74x393
endmodule
