// Digital circuit EEPROM PROGRAMMER.dig as structural Verilog
module EEPROM_PROGRAMMER (
  input  clk,
  input  [15:0] in_2,
  input  En,
  input  [3:0] Step,
  input  [6:0] Op,
  input  CF
);

  wire Clk_t, counter_1_ovf;
  wire [12:0] counter_1_out;

  Counter #(.Bits(13)) counter_1 (.en(1'b1), .C(Clk_t), .clr(counter_1_ovf), .out(counter_1_out), .ovf(counter_1_ovf));
  and and_1 (Clk_t, clk, En);
  EEPROMDualPort #(.AddrBits(13), .Bits(16)) eepromdualport_1 (
    .A({counter_1_out[12:11], Op, Step}), .Din(in_2), .str(1'b1), .C(Clk_t), .ld(1'b0));  // open: D

  // Notes on the sheet:
  //   clk: Hz: 100000
  //   Step: default 1
  //   Default: 0x007f
  //   Fetch: 0x727f
  //   EI: 0x807f
  //   JMP: 
  //   405f
  //   503f
  //   71f7
  //   70ef
  //   Skip JMP:
  //   027f    x2
  //   get addr:
  //   725f
  //   723f
  //   1: Ao
  //   2: Bo
  //   3: So
  //   4: CLo
  //   5: CHo
  //   6: 
  //   7: Ro
  //   contents of eepromdualport_1 (hex, n*v repeats v):
  //   727f,807f,8*7f,0,5*7f,727f,727c,807f,13*7f,727f,47d,3c7c,807f
  //   ,12*7f,727f,47d,307c,807f,12*7f,727f,727d,307c,807f,12*7f,727f
  //   ,405f,503f,71f7,70ef,807f,10*7f,727f,27f,27f,807f,12*7f,727f,405f
  //   ,503f,71f7,70ef,807f,10*7f,727f,311f,10fb,47e,307f,70fe,405f,503f
  //   ,71f7,70ef,807f,5*7f,727f,311f,10fb,47e,307f,70fe,27f,27f,807f
  //   ,7*7f,727f,725f,723f,70fd,307c,807f,10*7f,727f,725f,723f,70fd
  //   ,307c,807f,10*7f,727f,725f,723f,70fd,3c7c,807f,10*7f,727f,725f
  //   ,723f,70fd,347c,807f,10*7f,727f,725f,723f,70fc,807f,11*7f,727f
  //   ,725f,723f,10fb,807f,11*7f,727f,3f,45f,70dd,10fb,207e,45d,30fb
  //   ,105f,70fe,807f,5*7f,727f,3f,45d,70fe,3cfe,10fb,105f,70fc,807f
  //   ,7*7f,727f,47d,387f,807f,12*7f,727f,30fd,307f,807f,12*7f,727f
  //   ,725f,60fc,807f,12*7f,727f,311f,10fb,41d,70de,40fb,305e,50fb,205f
  //   ,30fb,405f,503f,71f7,70ef,311f,70fe,727f,311f,10fb,41d,70de,3c5e
  //   ,70ef,3c5e,70f7,205f,10fb,331f,72fe,807f,7f,7f,727f,107d,307c
  //   ,807f,12*7f,727f,107d,347f,8*307c,807f,4*7f,727f,807f,14*7f,727f
  //   ,107d,307c,807f,12*7f,727f,107d,8*307c,807f,5*7f,727f,727d,725f
  //   ,723f,20fb,807f,10*7f,727f,107d,307f,405f,503f,71f7,70ef,807f
  //   ,8*7f,727f,107d,307f,27f,27f,807f,10*7f,727f,725f,723f,70fd,3c7d
  //   ,807f,10*7f,727f,727d,3c7d,807f,12*7f,727f,725f,723f,71fd,70bf
  //   ,205f,70fc,807f,8*7f,727f,725f,723f,71fd,70bf,205f,10fb,807f,8*7f
  //   ,727f,41d,70de,40fb,305e,50fb,205f,30fb,405f,503f,71f7,70ef,807f
  //   ,7f,7f,7f,727f,41d,70de,3c5e,70ef,3c5e,70f7,205f,10fb,807f,6*7f
  //   ,727f,807f,14*7f,727f,807f,14*7f,727f,107d,317e,3c7c,807f,11*7f
  //   ,727f,807f,14*7f,727f,807f,14*7f,727f,807f,14*7f,727f,807f,14*7f
  //   ,727f,725f,723f,70fd,725f,723f,20fb,807f,8*7f,727f,807f,14*7f
  //   ,727f,807f,14*7f,727f,311f,10fb,725f,723f,70fc,347d,3cfb,311f
  //   ,70fe,807f,5*7f,727f,807f,14*7f,727f,807f,14*7f,727f,807f,14*7f
  //   ,727f,807f,14*7f,727f,807f,14*7f,727f,725f,723f,70fd,10fb,207e
  //   ,47d,3c7d,70fe,20fb,807f,5*7f,727f,725f,723f,70fd,10fb,47e,307d
  //   ,70fe,20fb,807f,6*7f,727f,807f,14*7f,727f,807f,14*7f,727f,807f
  //   ,14*7f,727f,807f,14*7f,727f,807f,14*7f,727f,807f,14*7f,727f,807f
  //   ,14*7f,727f,807f,14*7f,727f,807f,14*7f,727f,807f,14*7f,727f,807f
  //   ,14*7f,727f,807f,14*7f,727f,807f,14*7f,727f,807f,14*7f,727f,807f
  //   ,14*7f,727f,807f,14*7f,727f,807f,14*7f,727f,807f,14*7f,727f,807f
  //   ,14*7f,727f,807f,14*7f,727f,807f,14*7f,727f,807f,14*7f,727f,807f
  //   ,14*7f,727f,807f,14*7f,727f,807f,14*7f,727f,807f,14*7f,727f,807f
  //   ,14*7f,727f,807f,14*7f,727f,807f,14*7f,727f,807f,14*7f,727f,807f
  //   ,14*7f,727f,807f,14*7f,727f,807f,14*7f,727f,807f,14*7f,727f,807f
  //   ,14*7f,727f,807f,14*7f,727f,807f,14*7f,727f,807f,14*7f,727f,807f
  //   ,14*7f,727f,807f,14*7f,727f,807f,14*7f,727f,807f,14*7f,727f,807f
  //   ,14*7f,727f,807f,14*7f,727f,807f,14*7f,727f,807f,14*7f,727f,807f
  //   ,14*7f,727f,807f,14*7f,727f,807f,14*7f,727f,807f,14*7f,727f,807f
  //   ,14*7f,727f,807f,14*7f,727f,807f,14*7f,727f,807f,14*7f,727f,807f
  //   ,14*7f,727f,807f,14*7f,727f,807f,14*7f,727f,807f,14*7f,727f,807f
  //   ,14*7f,727f,807f,14*7f,727f,807f,14*7f,727f,807f,14*7f,727f,807f
  //   ,14*7f,727f,807f,14*7f,727f,807f,14*7f,727f,807f,14*7f,727f,707d
  //   ,311f,34fb,107d,727e,347e,70fd,307c,307c,807f,5*7f,727f,725f,723f
  //   ,70fd,307c,307c,807f,9*7f,727f,727d,307c,307c,807f,11*7f,727f
  //   ,725f,723f,10fd,307e,70fd,347c,807f,8*7f,727f,10fd,307e,727d,347c
  //   ,807f,10*7f,727f,10fd,307e,727d,347d,807f,10*7f,727f,807f,14*7f
  //   ,727f,807f,14*7f,727f,727c,807f,13*7f,727f,47d,3c7c,807f,12*7f
  //   ,727f,47d,307c,807f,12*7f,727f,727d,307c,807f,12*7f,727f,405f
  //   ,503f,71f7,70ef,807f,10*7f,727f,405f,503f,71f7,70ef,807f,10*7f
  //   ,727f,27f,27f,807f,12*7f,727f,311f,10fb,47e,307f,70fe,27f,27f
  //   ,807f,7*7f,727f,311f,10fb,47e,307f,70fe,405f,503f,71f7,70ef,807f
  //   ,5*7f,727f,725f,723f,70fd,307c,807f,10*7f,727f,725f,723f,70fd
  //   ,387c,807f,10*7f,727f,725f,723f,70fd,3c7c,807f,10*7f,727f,725f
  //   ,723f,70fd,3c7c,807f,10*7f,727f,725f,723f,70fc,807f,11*7f,727f
  //   ,725f,723f,10fb,807f,11*7f,727f,3f,45f,70dd,10fb,207e,45d,30fb
  //   ,105f,70fe,807f,5*7f,727f,3f,45d,70fe,3cfe,10fb,105f,70fc,807f
  //   ,7*7f,727f,47d,387f,807f,12*7f,727f,30fd,307f,807f,12*7f,727f
  //   ,725f,60fc,807f,12*7f,727f,311f,10fb,41d,70de,40fb,305e,50fb,205f
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endmodule
