// Digital circuit MAIN.dig as structural Verilog
module MAIN (
  input  Clk
);

  wire CF, nBoot, Ri, Ro, Rst_out;
  wire [3:0] Step;
  wire [7:0] A, B, Bank, Boot_ROM_d, CH, CL, IR, MH, ML;
  wire [12:0] cpu_1_address_bus;
  wire [15:13] cpu_1_address_bus_2;

  CPU cpu_1 (
    .Clk(Clk), .Rst(Rst_out), .Data_Bus(Boot_ROM_d), .A(A), .B(B), .CH(CH), .CL(CL), .MH(MH), .ML(ML),
    .IR(IR), .Step(Step), .CF(CF), .Boot(nBoot), .Ro(Ro), .Ri(Ri),
    .Address_Bus({cpu_1_address_bus_2, cpu_1_address_bus}), .Bank(Bank));
  Button #(.activeLow("true")) Rst (.out(Rst_out));
  EEPROM #(.AddrBits(13), .Bits(8)) Boot_ROM (
    .A(cpu_1_address_bus), .CS(~nBoot), .WE(~1'b1), .OE(~1'b0), .D(Boot_ROM_d));
  RAMSinglePortSel #(.AddrBits(16), .Bits(8)) ramsingleportsel_1 (
    .A({cpu_1_address_bus_2, cpu_1_address_bus}), .CS(~1'b0), .WE(~Ri), .OE(~Ro), .D(Boot_ROM_d));
  LED led_1 (.in(A[4]));
  LED led_2 (.in(A[5]));
  LED led_3 (.in(A[6]));
  LED led_4 (.in(A[7]));
  LED led_5 (.in(B[4]));
  LED led_6 (.in(B[5]));
  LED led_7 (.in(B[6]));
  LED led_8 (.in(B[7]));
  LED led_9 (.in(CH[4]));
  LED led_10 (.in(CH[5]));
  LED led_11 (.in(CH[6]));
  LED led_12 (.in(CH[7]));
  LED led_13 (.in(MH[4]));
  LED led_14 (.in(MH[5]));
  LED led_15 (.in(MH[6]));
  LED led_16 (.in(MH[7]));
  LED led_17 (.in(Step[0]));
  LED led_18 (.in(Step[1]));
  LED led_19 (.in(Step[2]));
  LED led_20 (.in(Step[3]));
  LED led_21 (.in(IR[4]));
  LED led_22 (.in(IR[5]));
  LED led_23 (.in(IR[6]));
  LED led_24 (.in(IR[7]));
  LED led_25 (.in(A[0]));
  LED led_26 (.in(A[1]));
  LED led_27 (.in(A[2]));
  LED led_28 (.in(A[3]));
  LED led_29 (.in(B[0]));
  LED led_30 (.in(B[1]));
  LED led_31 (.in(B[2]));
  LED led_32 (.in(B[3]));
  LED led_33 (.in(CH[0]));
  LED led_34 (.in(CH[1]));
  LED led_35 (.in(CH[2]));
  LED led_36 (.in(CH[3]));
  LED led_37 (.in(MH[0]));
  LED led_38 (.in(MH[1]));
  LED led_39 (.in(MH[2]));
  LED led_40 (.in(MH[3]));
  LED led_41 (.in(CF));
  LED led_42 (.in(IR[0]));
  LED led_43 (.in(IR[1]));
  LED led_44 (.in(IR[2]));
  LED led_45 (.in(IR[3]));
  LED led_46 (.in(CL[4]));
  LED led_47 (.in(CL[5]));
  LED led_48 (.in(CL[6]));
  LED led_49 (.in(CL[7]));
  LED led_50 (.in(ML[4]));
  LED led_51 (.in(ML[5]));
  LED led_52 (.in(ML[6]));
  LED led_53 (.in(ML[7]));
  LED led_54 (.in(CL[0]));
  LED led_55 (.in(CL[1]));
  LED led_56 (.in(CL[2]));
  LED led_57 (.in(CL[3]));
  LED led_58 (.in(ML[0]));
  LED led_59 (.in(ML[1]));
  LED led_60 (.in(ML[2]));
  LED led_61 (.in(ML[3]));

  // Notes on the sheet:
  //   Clk: Hz: 2147483647
  //   contents of Boot_ROM (hex, n*v repeats v):
  //   0,1,fe,f,ff,ff,f,ff,fe,5,6,1,244*0,20,80,3,2,0,0,15,d7,1,15,31
  //   ,1,15,4b,1,15,9b,2,15,3e,2,15,56,2,15,26,2,e,4,1,20,9,8,2e,1,e
  //   ,5,1,20,9,8,2e,1,5,f,1,5,2e,1,1c,80,4a,1,1c,9,3,fd,1,1,2c,4a,1
  //   ,2,fd,f,4,fd,36,4a,1,9,3b,1,16,0,1c,40,2,fd,1c,9,3,fd,1c,4,80
  //   ,1,1c,f,81,1,1,1,f,4,fd,35,3,fd,36,80,1,9,5d,1,1c,4,80,1,35,3
  //   ,fd,35,3,fd,35,3,fd,35,3,fd,36,81,1,9,5d,1,16,0,0,11,f,d3,1,11
  //   ,f,d2,1,11,17,17,17,f,3,fd,11,17,17,17,f,2,fd,f,d6,1,1,8,f,d5
  //   ,1,1,8,f,d4,1,2c,d6,1,2,fd,21,d2,1,17,7,b8,1,1c,1,4,fd,5,bc,1
  //   ,1c,0,4,fd,35,2,fd,36,d4,1,9,ad,1,2f,d2,1,35,3,fd,36,d5,1,9,a0
  //   ,1,16,5*0,1,4,10,1,0,10,e,4,1,17,17,17,a,22,2,f,24,2,1,0,b,23
  //   ,2,f,25,2,e,24,2,10,e,25,2,10,15,82,1,1,c,10,1,0,10,e,5,1,17,17,17
  //   ,a,22,2,f,24,2,1,0,b,23,2,f,25,2,e,24,2,10,e,25,2,10,15,82,1,16
  //   ,b6,2,0,0,e,0,1,18,20,40,8,3d,2,f,2,fd,e,1,1,18,f,3,fd,1c,1,4
  //   ,fd,16,e,0,1,18,20,40,8,55,2,f,2,fd,e,1,1,18,f,3,fd,1c,0,4,fd
  //   ,16,e,0,1,a,2,1,18,20,7f,7,69,2,e,2,1,27,f,2,1,e,0,1,a,2,1,f,0
  //   ,1,e,1,1,a,3,1,18,20,a,6,85,2,e,3,1,27,f,3,1,20,7f,7,91,2,e,3
  //   ,1,27,f,3,1,e,1,1,a,3,1,f,1,1,16,14,0,fe,1,8,a8,2,35,5,1,15,d7
  //   ,1,14,0,fe,2,8,b5,2,35,4,1,15,d7,1,16,0,3c,66,76,6e,66,66,3c,0
  //   ,8,18,38,18,18,18,7e,0,3c,66,66,e,1c,38,7e,0,7e,7e,6,3c,6,7e,7e
  //   ,0,e,1e,36,66,7e,6,6,0,7e,7e,60,7c,6,7e,7c,0,3c,7c,60,7c,66,66
  //   ,3c,0,7e,7e,6,c,c,18,18,0,3c,66,66,3c,66,66,3c,0,3e,66,66,3e,6,6,6
endmodule
