// Digital circuit RAM module.dig as structural Verilog
module RAM_module (
  input  [7:0] D,
  input  [15:0] Address,
  input  Ri,
  input  Ro
);

  wire not_1_out;

  RAMSinglePortSel #(.AddrBits(15), .Bits(8)) ramsingleportsel_1 (
    .A(Address[14:0]), .CS(~Address[15]), .WE(~Ri), .OE(~Ro), .D(D));
  RAMSinglePortSel #(.AddrBits(15), .Bits(8)) ramsingleportsel_2 (
    .A(Address[14:0]), .CS(~not_1_out), .WE(~Ri), .OE(~Ro), .D(D));
  not not_1 (not_1_out, Address[15]);
endmodule
