// Digital circuit ALU.dig as structural Verilog
module ALU (
  input  [7:0] A,
  input  [7:0] B,
  input  inv,
  input  ci,
  input  \nor ,
  input  Zero,
  output [7:0] Q,
  output F
);

  wire _7483_1_pin13, I0, I1, I2, I3, I4, I5, I6, I7, NOR0, NOR1, NOR2, NOR3, NOR4, NOR5, NOR6, NOR7, S0, S1,
       S2, S3, S4, S5, S6, S7;

  _7486 _7486_1 (
    .pin1(B[4]), .pin2(inv), .pin3(I4), .pin4(B[5]), .pin5(inv), .pin6(I5), .pin7(1'b0), .pin8(I6),
    .pin9(B[6]), .pin10(inv), .pin11(I7), .pin12(B[7]), .pin13(inv), .pin14(1'b1));
  _7486 _7486_2 (
    .pin1(B[0]), .pin2(inv), .pin3(I0), .pin4(B[1]), .pin5(inv), .pin6(I1), .pin7(1'b0), .pin8(I2),
    .pin9(B[2]), .pin10(inv), .pin11(I3), .pin12(B[3]), .pin13(inv), .pin14(1'b1));
  _7483 _7483_1 (
    .pin1(A[7]), .pin2(S6), .pin3(A[6]), .pin4(I6), .pin5(1'b1), .pin6(S5), .pin7(I5), .pin8(A[5]),
    .pin9(S4), .pin10(A[4]), .pin11(I4), .pin12(1'b0), .pin13(_7483_1_pin13), .pin14(F), .pin15(S7),
    .pin16(I7));
  _7483 _7483_2 (
    .pin1(A[3]), .pin2(S2), .pin3(A[2]), .pin4(I2), .pin5(1'b1), .pin6(S1), .pin7(I1), .pin8(A[1]),
    .pin9(S0), .pin10(A[0]), .pin11(I0), .pin12(1'b0), .pin13(ci), .pin14(_7483_1_pin13), .pin15(S3),
    .pin16(I3));
  _7402 _7402_1 (
    .pin1(NOR4), .pin2(A[4]), .pin3(I4), .pin4(NOR5), .pin5(A[5]), .pin6(I5), .pin7(1'b0), .pin8(A[6]),
    .pin9(I6), .pin10(NOR6), .pin11(A[7]), .pin12(I7), .pin13(NOR7), .pin14(1'b1));
  _7402 _7402_2 (
    .pin1(NOR0), .pin2(A[0]), .pin3(I0), .pin4(NOR1), .pin5(A[1]), .pin6(I1), .pin7(1'b0), .pin8(A[2]),
    .pin9(I2), .pin10(NOR2), .pin11(A[3]), .pin12(I3), .pin13(NOR3), .pin14(1'b1));
  _74157 _74157_1 (
    .pin1(\nor ), .pin2(S4), .pin3(NOR4), .pin4(Q[4]), .pin5(S5), .pin6(NOR5), .pin7(Q[5]), .pin8(1'b0),
    .pin9(Q[6]), .pin10(NOR6), .pin11(S6), .pin12(Q[7]), .pin13(NOR7), .pin14(S7), .pin15(Zero), .pin16(1'b1));
  _74157 _74157_2 (
    .pin1(\nor ), .pin2(S0), .pin3(NOR0), .pin4(Q[0]), .pin5(S1), .pin6(NOR1), .pin7(Q[1]), .pin8(1'b0),
    .pin9(Q[2]), .pin10(NOR2), .pin11(S2), .pin12(Q[3]), .pin13(NOR3), .pin14(S3), .pin15(Zero), .pin16(1'b1));

  // Other names for the same wires on the sheet: Co = F; inv_b = inv; S = \nor 
endmodule
