// Digital circuit Controller.dig as structural Verilog
module Controller (
  output [7:0] Q
);

  Button UP (.out(Q[7]));
  Button LEFT (.out(Q[6]));
  Button DOWN (.out(Q[5]));
  Button RIGHT (.out(Q[4]));
  Button J (.out(Q[3]));
  Button K (.out(Q[2]));
  Button Z (.out(Q[1]));
  Button X (.out(Q[0]));
endmodule
