// Digital circuit IO.dig as structural Verilog
module IO (
  input  Po,
  input  Clk,
  input  [15:0] A,
  input  [7:0] D,
  output [7:0] Q,
  output [7:0] Bank
);

  wire nand_1_out, not_1_out, not_2_out, not_3_out;
  wire [7:0] controller_1_q, decoder_1_q, decoder_2_q;

  nand nand_1 (nand_1_out, A[8], not_1_out, A[10], A[11], A[13], A[14], A[15], A[12]);
  not not_1 (not_1_out, A[9]);
  decoder decoder_1 (.A(A[0]), .B(A[1]), .C(A[2]), .en1(Po), .en2(1'b0), .en3(1'b1), .Q(decoder_1_q));
  decoder decoder_2 (.A(A[0]), .B(A[1]), .C(A[2]), .en1(nand_1_out), .en2(1'b0), .en3(1'b1), .Q(decoder_2_q));
  not not_2 (not_2_out, decoder_2_q[0]);
  Controller controller_1 (.Q(controller_1_q));
  driver driver_1 (.En(decoder_1_q[0]), .D(controller_1_q), .Q(Q));
  Keyboard keyboard_1 (.Clk(Clk), .En(not_3_out), .D(Q));
  not not_3 (not_3_out, decoder_1_q[1]);
  Terminal #(.termWidth(20), .termHeight(5)) terminal_1 (.D(D), .C(Clk), .en(not_2_out));
  \reg  u_Bank (.D(D), .Clk(Clk), .En(decoder_2_q[1]), .Q(Bank));  // open: V
  Screen_Cicuitry screen_cicuitry_1 (.Clk(Clk), .xi(decoder_2_q[2]), .yi(decoder_2_q[3]), .si(decoder_2_q[4]), .D(D));

  // Other names for the same wires on the sheet: Data[7:0] = D; nPo = Po
endmodule
