// Digital circuit bus control.dig as structural Verilog
module bus_control (
  input  inv,
  input  OS0,
  input  OS1,
  input  OS2,
  input  boot,
  output [7:0] Q
);

  wire not_1_out, or_1_out, or_2_out, or_3_out;
  wire [7:0] multiplexer_1_out;

  or or_1 (or_1_out, boot, OS2);
  or or_2 (or_2_out, OS1, OS0);
  or or_3 (or_3_out, or_1_out, or_2_out);
  Multiplexer #(.Bits(8)) multiplexer_1 (.sel(inv), .in_0(8'hfe), .in_1({8{1'b1}}), .out(multiplexer_1_out));
  assign Q = not_1_out ? multiplexer_1_out : 8'bz;  // Driver driver_1
  not not_1 (not_1_out, or_3_out);

  // Notes on the sheet:
  //   UNNEEDED IN IRL BUILD SIMPLY 
  //   HOOK BOTTOM BIT OF BUS THROUGH 
  //   A PULL RESISTOR TO "INV" LINE
endmodule
