// Digital circuit count-16.dig as structural Verilog
module count_16 (
  input  [7:0] D,
  input  JL,
  input  JH,
  input  En,
  input  Clk,
  input  Rst,
  output [7:0] QL,
  output [7:0] VL,
  output [7:0] QH,
  output [7:0] VH,
  output Co
);

  wire H_pin15, L_2_pin15, L_pin15;

  _74161 L (
    .pin1(Rst), .pin2(Clk), .pin3(D[0]), .pin4(D[1]), .pin5(D[2]), .pin6(D[3]), .pin7(En), .pin8(1'b0),
    .pin9(JL), .pin10(1'b1), .pin11(QL[3]), .pin12(QL[2]), .pin13(QL[1]), .pin14(QL[0]), .pin15(L_pin15),
    .pin16(1'b1));
  _74161 H (
    .pin1(Rst), .pin2(Clk), .pin3(D[4]), .pin4(D[5]), .pin5(D[6]), .pin6(D[7]), .pin7(En), .pin8(1'b0),
    .pin9(JL), .pin10(L_pin15), .pin11(QL[7]), .pin12(QL[6]), .pin13(QL[5]), .pin14(QL[4]), .pin15(H_pin15),
    .pin16(1'b1));
  _74161 L_2 (
    .pin1(Rst), .pin2(Clk), .pin3(D[0]), .pin4(D[1]), .pin5(D[2]), .pin6(D[3]), .pin7(En), .pin8(1'b0),
    .pin9(JH), .pin10(H_pin15), .pin11(QH[3]), .pin12(QH[2]), .pin13(QH[1]), .pin14(QH[0]),
    .pin15(L_2_pin15), .pin16(1'b1));
  _74161 H_2 (
    .pin1(Rst), .pin2(Clk), .pin3(D[4]), .pin4(D[5]), .pin5(D[6]), .pin6(D[7]), .pin7(En), .pin8(1'b0),
    .pin9(JH), .pin10(L_2_pin15), .pin11(QH[7]), .pin12(QH[6]), .pin13(Co), .pin14(QH[4]), .pin16(1'b1));  // open: pin15

  assign QH[5] = Co;
  assign VH = {QH[7:6], Co, QH[4:0]};
  assign VL = QL;
endmodule
