// Digital circuit decoder.dig as structural Verilog
module decoder (
  input  A,
  input  B,
  input  C,
  input  en1,
  input  en2,
  input  en3,
  output [7:0] Q
);

  _74138 _74138_1 (
    .pin1(A), .pin2(B), .pin3(C), .pin4(en1), .pin5(en2), .pin6(en3), .pin7(Q[7]), .pin8(1'b0), .pin9(Q[6]),
    .pin10(Q[5]), .pin11(Q[4]), .pin12(Q[3]), .pin13(Q[2]), .pin14(Q[1]), .pin15(Q[0]), .pin16(1'b1));
endmodule
